# Fritzing sketch Projek KP 2 (saved by Fritzing 0.9.5d)
# 18650 Li-ion Battery: CC-BY Dr Kristofer Chan, King's College London/Remote-research.org

parts:
  U1 = LM2596 step down module
  DHT1 = DHT22 Humidity and Temperature Sensor
  Part1 = LCD1602-I2C
  BAT1 = 18650 Li-ion Battery [package=battery-18650]
  BAT2 = 18650 Li-ion Battery [package=battery-18650]
  Part2 = Adafruit INA219 [part_number="Adafruit #904"]
  SD_card_module1 = SD Card Module
  M1 = DOIT Esp32 DevKit v1 (30 pins long, 11 pins width) [part_number=ESP32S-PIN30]
  Mod1 = KY-012 Active Buzzer Module [package="Breakout board"]

nets:
  N1: U1.IN+, BAT1.+, Part2.VIN+
  GND: U1.IN-, U1.OUT-, DHT1.GND, Part1.GND, BAT2.-, Part2.GND, SD_card_module1.GND, M1.GND, Mod1.-
  VCC: U1.OUT+, Part1.VCC, SD_card_module1.+5, M1.VIN, Mod1.NC
  VDD: DHT1.VDD, Part2.VCC, M1.3V3
  N2: DHT1.DATA, M1.D4
  N3: Part1.SDA, Part2.SDA, M1.D21
  N4: Part1.SCL, Part2.SCL, M1.D22
  N5: BAT1.-, BAT2.+
  N6: SD_card_module1.CS, M1.D5
  N7: SD_card_module1.MOSI, M1.D23
  N8: SD_card_module1.SCK, M1.D18
  N9: SD_card_module1.MISO, M1.D19
  N10: M1.D12, Mod1.S

custom parts:
  LM2596 step down module: LM2596 DC-DC step down power supply module 3 A.
  LCD1602-I2C: A standard character display, usually with 2x16 characters. Comes in many colors with LCM1602 IIC attached.
  18650 Li-ion Battery: 18650 li-ion Battery Standard 18650 battery with interactive connectors Creative Common Attribution 4.0 International (CC-BY 4.0) license. Any use of this part requires attribution of Dr Kristofer Chan, Department of Geography, King's College London. Contact kristofer.chan [at] kcl.ac.uk OR kris [at] remote-research.org for further information.
  Adafruit INA219: This breakout board will solve all your power-monitoring problems. Instead of struggling with two multimeters, you can just use the handy INA219B chip on this breakout to both measure both the high side voltage and DC current draw over I2C with 1% precision. Most current-measuring devices such as our current panel meter are only good for low side measuring. That means that unless you want to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
  SD Card Module: SD Card Module Slot Socket Reader For Arduino ARM MCU
  DOIT Esp32 DevKit v1 (30 pins long, 11 pins width): The DOIT Esp32 DevKit v1 is one of the development board created by DOIT to evaluate the ESP-WROOM-32 module. It is based on the ESP32 microcontroller that boasts Wifi, Bluetooth, Ethernet and Low Power support all in a single chip. (vanepp) made breadboard work, adjusted pin numbering and labels and reduced size of schematic and cleaned up pcb. This chip is 30pins long (2 x15) and 11 pins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
  KY-012 Active Buzzer Module: Active Piezoelectric Buzzer Module KY-012, it produces single-tone sound when signal is high. (Special thanks to vanepp for fixing the PCB holes and other errors)
